# Fritzing sketch puertadesalida (saved by Fritzing 0.9.2b)
breadboards: 1

parts:
  Parte1 = Arduino Uno (Rev3)
  LED1 = smd LED [color="Red (633nm)" package="0603 [SMD]"]
  LED2 = LED - 5mm [color="Green (570nm)" package="5 mm [THT]"]
  U8 = RELAY [package=relay-jzc]
  Grove1 = Grove Light Sensor
  Grove2 = Grove Light Sensor
  Grove3 = Grove Light Sensor
  Grove4 = Grove Light Sensor
  Grove5 = Grove Light Sensor
  Grove6 = Grove Light Sensor
  Grove7 = Grove Light Sensor
  Grove8 = Grove Light Sensor

nets:
  N1: Parte1.D8, Grove7.SIG
  N2: Parte1.D9_PWM, Grove8.SIG
  N3: Parte1.D10_PWM/SS, LED1.cathode
  N4: Parte1.D12/MISO, U8.NO
  N5: Parte1.D13/SCK, LED2.cathode
  N6: Parte1.D2, Grove1.SIG
  N7: Parte1.D3_PWM, Grove2.SIG
  N8: Parte1.D4, Grove3.SIG
  N9: Parte1.D5_PWM, Grove4.SIG
  N10: Parte1.D6_PWM, Grove5.SIG
  N11: Parte1.D7, Grove6.SIG
  VCC: Parte1.5V, U8.COIL2, Grove1.VCC, Grove2.VCC, Grove3.VCC, Grove4.VCC, Grove5.VCC, Grove6.VCC, Grove7.VCC, Grove8.VCC
  GND: Parte1.GND, LED1.anode, LED2.anode, U8.NC, Grove1.GND, Grove2.GND, Grove3.GND, Grove4.GND, Grove5.GND, Grove6.GND, Grove7.GND, Grove8.GND
