# Fritzing sketch tanquedecombustible (saved by Fritzing 0.9.2b)
breadboards: 1

parts:
  Parte1 = Arduino Uno (Rev3)
  LED1 = LED - 5mm [color="Red (633nm)" package="5 mm [THT]"]  # not connected
  LED2 = smd LED [color="Red (633nm)" package="0805 [SMD]"]
  J2 = Infrared Proximity Sensor
  J3 = Infrared Proximity Sensor

nets:
  N1: Parte1.D8, J3.Vout
  N2: Parte1.D6_PWM, LED2.cathode
  N3: Parte1.D7, J2.Vout
  5V: Parte1.5V, J2.Vcc
  GND: Parte1.GND, LED2.anode, J2.GND, J3.GND
